# Fritzing sketch dht11 and esp32 (saved by Fritzing 0.9.10b)
breadboards: 1

parts:
  ESP32_huzzah = Adafruit HUZZAH32 ESP32 Feather [part_number="Adafruit #3405"]
  DHT1 = Humidity and Temperature Sensor DHT11
  R1 = Resistor [tolerance=±5% power=0.25 resistance=10k package=THT]

nets:
  N1: ESP32_huzzah.SCK, ESP32_huzzah.GND, DHT1.Data-signal, R1.Pin_1
  N2: DHT1.Vcc, R1.Pin_0

custom parts:
  Humidity and Temperature Sensor DHT11: Digital relative humidity & temperature sensor DHT11
